# Fritzing sketch sensor_schematic (saved by Fritzing 0.9.3b)

parts:
  U1 = ESP32-38PinWide [part_number=ESP32-38PinWide]
  TCS1 = TCS3200
  Part1 = MQ-7 breakout
  Part2 = MQ-9 breakout
  Part3 = MQ-7 breakout
  Part4 = MQ-3 breakout

nets:
  VCC: U1.3.3, TCS1.VCC, TCS1.S1, TCS1.S0, TCS1.LED, Part1.VCC, Part2.VCC, Part3.VCC, Part4.VCC
  N1: U1.GPIO12, Part1.AO
  N2: U1.GPIO13, Part4.AO
  N3: U1.GPIO15, Part2.AO
  N4: U1.GPIO2, Part3.AO
  N5: U1.GPIO0, TCS1.S2
  N6: U1.GPIO4, TCS1.S3
  N7: U1.GPIO16, TCS1.OUT
  GND: U1.GND, TCS1.GND, Part1.GND, Part2.GND, Part3.GND, Part4.GND

custom parts:
  ESP32-38PinWide: Generic 38-Pin ESP32 with wide format (only access to one side of pins on a breadboard) based on Stephen Lilley's HiLetgo ESP-WROOM-32 ESP32 ESP-32S Development Board.
  TCS3200: COLOR SENSING TCS3200
  MQ-7 breakout: SKU: 101282
  MQ-9 breakout: SKU: 101284
  MQ-3 breakout: Alcohol sensor is capable of detecting alcohol (ethanol) particles on itself and gives the information in digital form back to us to manipulate with it. SKU:101251 • Voltage: 5V DC • Power: max 750mW • Measurement range: 0.04-4mg/L
